# Fritzing sketch PCB Design (saved by Fritzing 0.9.3b)
circuit board: 5.1006cm x 6.74838cm
breadboards: 1

parts:
  TPA2016 = Adafruit Stereo 2.8W Class D Audio Amplifier - I2C Control AGC - TPA2016 [part_number="Adafruit #1712"]
  Raspberry_Pi_1 = Raspberry Pi 3 [part_number=RPI-3-V1.2]

nets:
  VDD: TPA2016.VDD, Raspberry_Pi_1.5V
  GND: TPA2016.GND, Raspberry_Pi_1.GND
  N1: TPA2016.SCL, Raspberry_Pi_1.GPIO3
  N2: TPA2016.SDA, Raspberry_Pi_1.GPIO2

custom parts:
  Adafruit Stereo 2.8W Class D Audio Amplifier - I2C Control AGC - TPA2016: A mini class D with AGC and I2C control? Yes please! This incredibly small stereo amplifier is surprisingly powerful. It is able to deliver 2 x 2.8W channels into 4 ohm impedance speakers (@ 10% THD) and it has a i2c control interface as well as an AGC (automatic gain control) system to keep your audio from clipping or distorting. If you don't want to use I2C to control it, it does start up on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
